# Fritzing sketch Untitled Sketch 3 (saved by Fritzing 0.9.3b)
circuit board: 10cm x 6cm
breadboards: 1

parts:
  DHT3 = DHT11 Humitidy and Temperature Sensor (3 pins)
  U4 = NodeMCU V1.0
  LB = LED - 3mm [color="Blue (525nm)" package="3 mm [THT]"]
  LG = LED - 3mm [color="Green (555nm)" package="3 mm [THT]"]
  LR = LED - 3mm [color="Red (660nm)" package="3 mm [THT]"]

nets:
  N1: DHT3.DATA, U4.3V3
  N2: DHT3.VDD, U4.D2
  GND: DHT3.GND, U4.GND, LB.cathode, LG.cathode, LR.cathode
  N3: U4.D0, LB.anode
  N4: U4.D1, LG.anode
  N5: U4.D5, LR.anode

custom parts:
  DHT11 Humitidy and Temperature Sensor (3 pins): DHT11 Humidity and Temperature Sensor (3 pins) from the design created by John De Cristofaro for Adafruit Industries.
  NodeMCU V1.0: ESP8266 based NodeMCU
