# Fritzing sketch new (saved by Fritzing 0.9.3b)
circuit board: 8.46667cm x 5.64444cm
breadboards: 1

parts:
  LR = LED - 5mm [color="Red (633nm)" package="5 mm [THT]"]
  LB = LED - 5mm [color="Blue (525nm)" package="5 mm [THT]"]
  R100 = Resistor [tolerance=±5% resistance=100 package=THT]
  U1 = NodeMCU V1.0
  part = KY-015 Temperature & Humidity Sensor Module [package="Breakout board"]

nets:
  N1: LR.cathode, LB.cathode, U1.GND, part.-
  N2: LR.anode, R100.Pin_1
  N3: LB.anode, U1.D0
  N4: R100.Pin_0, U1.D5
  N5: U1.D2, part.Vin
  N6: U1.3V3, part.S

custom parts:
  NodeMCU V1.0: ESP8266 based NodeMCU
  KY-015 Temperature & Humidity Sensor Module: KY-015 temperature and humidity sensor module, provides a low-latency serial interface to measure humidity and temperature.
